// Logisim project lab1_part1.circ as structural Verilog: 1 circuit, main circuit main
module main (
  input  Y,
  input  S,
  input  X
);

  wire n7408_2_pin1, n7432_1_pin1, n7432_1_pin2;

  _7408 u_7408_1 (.pin1(Y), .pin2(S));  // open: pin3, pin4, pin5, pin6, pin13, pin12, pin11, pin10, pin9, pin8
  _7404 u_7404_1 (.pin1(S));  // open: pin2, pin3, pin4, pin5, pin6, pin13, pin12, pin11, pin10, pin9, pin8
  _7432 u_7432_1 (
    .pin1(n7432_1_pin1), .pin2(n7432_1_pin2));  // open: pin3, pin4, pin5, pin6, pin13, pin12, pin11, pin10, pin9, pin8
  _7408 u_7408_2 (
    .pin1(n7408_2_pin1), .pin2(X));  // open: pin3, pin4, pin5, pin6, pin13, pin12, pin11, pin10, pin9, pin8
endmodule
