// Logisim project lab1_part3.circ as structural Verilog: 1 circuit, main circuit main
module main (
  input  X,
  input  S,
  input  Y,
  output f
);

  wire and_1_out, and_2_out, not_1_out;

  not not_1 (not_1_out, S);
  and and_1 (and_1_out, X, not_1_out);
  and and_2 (and_2_out, S, Y);
  or or_1 (f, and_1_out, and_2_out);
endmodule
