// Logisim project lab2_part1.circ as structural Verilog: 3 circuits, main circuit main
module main (
  input  u,
  input  v,
  input  w,
  input  x,
  input  s1,
  input  s0,
  output m
);

  mux4to1 mux4to1_1 (.a(u), .b(v), .c(w), .d(x), .s1(s1), .s2(s0), .f(m));
endmodule

module mux2to1 (
  input  x,
  input  y,
  input  f,
  output O
);

  wire and_1_out, and_2_out, not_1_out;

  not not_1 (not_1_out, f);
  and and_1 (and_1_out, y, f);
  or or_1 (O, and_1_out, and_2_out);
  and and_2 (and_2_out, x, not_1_out);
endmodule

module mux4to1 (
  input  a,
  input  b,
  input  c,
  input  d,
  input  s1,
  input  s2,
  output f
);

  wire mux2to1_1_o, mux2to1_2_o;

  mux2to1 mux2to1_1 (.x(a), .y(b), .f(s1), .O(mux2to1_1_o));
  mux2to1 mux2to1_2 (.x(c), .y(d), .f(s1), .O(mux2to1_2_o));
  mux2to1 mux2to1_3 (.x(mux2to1_1_o), .y(mux2to1_2_o), .f(s2), .O(f));
endmodule
