// Logisim project lab4_part1.circ as structural Verilog: 20 circuits, main circuit main
module main (
  input  [3:0] A,
  input  [2:0] op,
  input  CLK
);

  wire hex_decoder_1_s0, hex_decoder_1_s1, hex_decoder_1_s2, hex_decoder_1_s3, hex_decoder_1_s4,
       hex_decoder_1_s5, hex_decoder_1_s6, hex_decoder_2_s0, hex_decoder_2_s1, hex_decoder_2_s2,
       hex_decoder_2_s3, hex_decoder_2_s4, hex_decoder_2_s5, hex_decoder_2_s6, hex_decoder_3_s0,
       hex_decoder_3_s1, hex_decoder_3_s2, hex_decoder_3_s3, hex_decoder_3_s4, hex_decoder_3_s5,
       hex_decoder_3_s6;
  wire [7:0] alu_1_aluout, ALUreg_q;

  HEX_DECODER hex_decoder_1 (
    .in_1(A), .S0(hex_decoder_1_s0), .S1(hex_decoder_1_s1), .S2(hex_decoder_1_s2), .S3(hex_decoder_1_s3),
    .S4(hex_decoder_1_s4), .S5(hex_decoder_1_s5), .S6(hex_decoder_1_s6));
  ALU alu_1 (.A(A), .B(ALUreg_q[3:0]), .op(op), .ALUout(alu_1_aluout));
  Register ALUreg (.D(alu_1_aluout), .clk(CLK), .Q(ALUreg_q));  // open: en, clr
  _7_Segment_Display u_7_segment_display_1 (
    .g(hex_decoder_1_s6), .f(hex_decoder_1_s5), .a(hex_decoder_1_s0), .b(hex_decoder_1_s1),
    .e(hex_decoder_1_s4), .d(hex_decoder_1_s3), .c(hex_decoder_1_s2));  // open: dp
  HEX_DECODER hex_decoder_2 (
    .in_1(ALUreg_q[3:0]), .S0(hex_decoder_2_s0), .S1(hex_decoder_2_s1), .S2(hex_decoder_2_s2),
    .S3(hex_decoder_2_s3), .S4(hex_decoder_2_s4), .S5(hex_decoder_2_s5), .S6(hex_decoder_2_s6));
  HEX_DECODER hex_decoder_3 (
    .in_1(ALUreg_q[7:4]), .S0(hex_decoder_3_s0), .S1(hex_decoder_3_s1), .S2(hex_decoder_3_s2),
    .S3(hex_decoder_3_s3), .S4(hex_decoder_3_s4), .S5(hex_decoder_3_s5), .S6(hex_decoder_3_s6));
  _7_Segment_Display HEX_ALU0 (
    .g(hex_decoder_2_s6), .f(hex_decoder_2_s5), .a(hex_decoder_2_s0), .b(hex_decoder_2_s1),
    .e(hex_decoder_2_s4), .d(hex_decoder_2_s3), .c(hex_decoder_2_s2));  // open: dp
  _7_Segment_Display HEX_ALU1 (
    .g(hex_decoder_3_s6), .f(hex_decoder_3_s5), .a(hex_decoder_3_s0), .b(hex_decoder_3_s1),
    .e(hex_decoder_3_s4), .d(hex_decoder_3_s3), .c(hex_decoder_3_s2));  // open: dp
endmodule

module full_adder (
  input  A,
  input  B,
  input  Cin,
  output S,
  output Cout
);

  wire and_1_out, and_2_out, and_3_out, and_4_out, and_5_out, and_6_out, and_7_out, not_1_out, not_2_out,
       not_3_out;

  not not_1 (not_1_out, A);
  not not_2 (not_2_out, B);
  not not_3 (not_3_out, Cin);
  and and_1 (and_1_out, not_1_out, not_2_out, Cin);
  and and_2 (and_2_out, not_1_out, B, not_3_out);
  and and_3 (and_3_out, A, not_2_out, not_3_out);
  and and_4 (and_4_out, A, B, Cin);
  and and_5 (and_5_out, A, B);
  and and_6 (and_6_out, A, Cin);
  and and_7 (and_7_out, B, Cin);
  or or_1 (S, and_1_out, and_2_out, and_3_out, and_4_out);
  or or_2 (Cout, and_5_out, and_6_out, and_7_out);
endmodule

module ripple_carry4 (
  input  Cin,
  input  [3:0] A,
  input  [3:0] B,
  output [3:0] S,
  output Cout
);

  wire full_adder_1_cout, full_adder_2_cout, full_adder_3_cout;

  full_adder full_adder_1 (.A(A[0]), .B(B[0]), .Cin(Cin), .S(S[0]), .Cout(full_adder_1_cout));
  full_adder full_adder_2 (.A(A[1]), .B(B[1]), .Cin(full_adder_1_cout), .S(S[1]), .Cout(full_adder_2_cout));
  full_adder full_adder_3 (.A(A[2]), .B(B[2]), .Cin(full_adder_2_cout), .S(S[2]), .Cout(full_adder_3_cout));
  full_adder full_adder_4 (.A(A[3]), .B(B[3]), .Cin(full_adder_3_cout), .S(S[3]), .Cout(Cout));
endmodule

module op0 (
  input  [3:0] A,
  output [7:0] OPout
);

  wire ripple_carry4_1_cout;
  wire [3:0] ripple_carry4_1_s;
  wire [4:0] bit_extender_1_out;

  ripple_carry4 ripple_carry4_1 (.Cin(1'b1), .A(A), .B(4'b0000), .S(ripple_carry4_1_s), .Cout(ripple_carry4_1_cout));
  assign bit_extender_1_out = {{1{ripple_carry4_1_cout}}, ripple_carry4_1_s};  // Bit_Extender bit_extender_1
  assign OPout = {{3{1'b0}}, bit_extender_1_out};  // Bit_Extender bit_extender_2
endmodule

module op1 (
  input  [3:0] A,
  input  [3:0] B,
  output [7:0] OPout
);

  wire ripple_carry4_1_cout;
  wire [3:0] ripple_carry4_1_s;
  wire [4:0] bit_extender_1_out;

  ripple_carry4 ripple_carry4_1 (.Cin(1'b0), .A(A), .B(B), .S(ripple_carry4_1_s), .Cout(ripple_carry4_1_cout));
  assign bit_extender_1_out = {{1{ripple_carry4_1_cout}}, ripple_carry4_1_s};  // Bit_Extender bit_extender_1
  assign OPout = {{3{1'b0}}, bit_extender_1_out};  // Bit_Extender bit_extender_2
endmodule

module op2 (
  input  [3:0] A,
  input  [3:0] B,
  output [7:0] OPout
);

  wire adder_1_cout;
  wire [3:0] adder_1_out;
  wire [4:0] bit_extender_1_out;

  Adder #(.width(4)) adder_1 (.a(A), .b(B), .out(adder_1_out), .cout(adder_1_cout));  // open: cin
  assign bit_extender_1_out = {{1{adder_1_cout}}, adder_1_out};  // Bit_Extender bit_extender_1
  assign OPout = {{3{1'b0}}, bit_extender_1_out};  // Bit_Extender bit_extender_2
endmodule

module op3 (
  input  [3:0] A,
  input  [3:0] B,
  output [7:0] OPout
);

  assign OPout[3:0] = A ^ B;  // XOR_Gate xor_1, 4 bits wide
  assign OPout[7:4] = A | B;  // OR_Gate or_1, 4 bits wide
endmodule

module op4 (
  input  [3:0] A,
  input  [3:0] B,
  output [7:0] OPout
);

  wire or_1_out;

  or or_1 (or_1_out, A[0], A[1], A[2], A[3], B[0], B[1], B[2], B[3]);
  assign OPout = {{7{1'b0}}, or_1_out};  // Bit_Extender bit_extender_1
endmodule

module op5 (
  input  [3:0] A,
  input  [3:0] B,
  output [7:0] OPout
);

  wire [8:0] bit_extender_1_out;
  wire [8:8] shifter_1_out;

  assign bit_extender_1_out = {{5{B[3]}}, B};  // Bit_Extender bit_extender_1
  Shifter #(.width(9)) shifter_1 (.in(bit_extender_1_out), .\dist (A), .out({shifter_1_out[8], OPout}));
endmodule

module ALU (
  input  [3:0] A,
  input  [3:0] B,
  input  [2:0] op,
  output [7:0] ALUout
);

  wire [7:0] op0_1_opout, op1_1_opout, op2_1_opout, op3_1_opout, op4_1_opout, op5_1_opout, op6_1_opout,
       op7_1_opout;

  op0 op0_1 (.A(A), .OPout(op0_1_opout));
  op1 op1_1 (.A(A), .B(B), .OPout(op1_1_opout));
  op2 op2_1 (.A(A), .B(B), .OPout(op2_1_opout));
  op3 op3_1 (.A(A), .B(B), .OPout(op3_1_opout));
  op4 op4_1 (.A(A), .B(B), .OPout(op4_1_opout));
  op5 op5_1 (.A(A), .B(B), .OPout(op5_1_opout));
  op6 op6_1 (.A(A), .B(B), .OPout(op6_1_opout));
  op7 op7_1 (.A(A), .B(B), .OPout(op7_1_opout));
  Multiplexer #(.enable("false"), .select(3), .width(8)) multiplexer_1 (
    .in0(op0_1_opout), .in1(op1_1_opout), .in2(op2_1_opout), .in3(op3_1_opout), .in4(op4_1_opout),
    .in5(op5_1_opout), .in6(op6_1_opout), .in7(op7_1_opout), .out(ALUout), .sel(op));
endmodule

module HEX6 (
  input  D3,
  input  D2,
  input  D1,
  input  D0,
  output S6
);

  wire and_1_out, and_2_out, and_3_out, not_1_out, not_2_out, not_3_out;

  not not_1 (not_1_out, D2);
  not not_2 (not_2_out, D1);
  not not_3 (not_3_out, D0);
  and and_1 (and_1_out, not_1_out, D1);
  and and_2 (and_2_out, D2, not_2_out);
  and and_3 (and_3_out, D2, not_3_out);
  or or_1 (S6, and_1_out, and_2_out, and_3_out, D3);
endmodule

module HEX1 (
  input  D3,
  input  D2,
  input  D1,
  input  D0,
  output s1
);

  wire and_1_out, and_2_out, and_3_out, and_4_out, and_5_out, not_1_out, not_2_out, not_3_out, not_4_out;

  not not_1 (not_1_out, D3);
  not not_2 (not_2_out, D2);
  not not_3 (not_3_out, D1);
  not not_4 (not_4_out, D0);
  and and_1 (and_1_out, not_1_out, not_2_out);
  and and_2 (and_2_out, not_1_out, not_3_out, not_4_out);
  and and_3 (and_3_out, not_2_out, not_4_out);
  and and_4 (and_4_out, not_1_out, D1, D0);
  and and_5 (and_5_out, D3, not_3_out, D0);
  or or_1 (s1, and_1_out, and_2_out, and_3_out, and_4_out, and_5_out);
endmodule

module HEX2 (
  input  D3,
  input  D2,
  input  D1,
  input  D0,
  output S2
);

  wire and_1_out, and_2_out, and_3_out, and_4_out, and_5_out, not_1_out, not_2_out, not_3_out;

  not not_1 (not_1_out, D3);
  not not_2 (not_2_out, D2);
  not not_3 (not_3_out, D1);
  and and_1 (and_1_out, not_2_out, not_3_out);
  and and_2 (and_2_out, not_2_out, D0);
  and and_3 (and_3_out, not_3_out, D0);
  and and_4 (and_4_out, not_1_out, D2);
  and and_5 (and_5_out, D3, not_2_out);
  or or_1 (S2, and_1_out, and_2_out, and_3_out, and_4_out, and_5_out);
endmodule

module HEX3 (
  input  D3,
  input  D2,
  input  D1,
  input  D0,
  output S3
);

  wire and_1_out, and_2_out, and_3_out, and_4_out, and_5_out, and_6_out, not_1_out, not_2_out, not_3_out,
       not_4_out;

  not not_1 (not_1_out, D3);
  not not_2 (not_2_out, D2);
  not not_3 (not_3_out, D1);
  not not_4 (not_4_out, D0);
  and and_1 (and_1_out, not_1_out, not_2_out, not_4_out);
  and and_2 (and_2_out, not_1_out, D1, not_4_out);
  and and_3 (and_3_out, not_2_out, D1, D0);
  and and_4 (and_4_out, D2, not_3_out, D0);
  and and_5 (and_5_out, D2, D1, not_4_out);
  and and_6 (and_6_out, D3, not_3_out);
  or or_1 (S3, and_1_out, and_2_out, and_3_out, and_4_out, and_5_out, and_6_out);
endmodule

module HEX4 (
  input  D3,
  input  D2,
  input  D1,
  input  D0,
  output S4
);

  wire and_1_out, and_2_out, and_3_out, and_4_out, not_1_out, not_2_out;

  not not_1 (not_1_out, D2);
  not not_2 (not_2_out, D0);
  and and_1 (and_1_out, not_1_out, not_2_out);
  and and_2 (and_2_out, D1, not_2_out);
  and and_3 (and_3_out, D3, D1);
  and and_4 (and_4_out, D3, D2);
  or or_1 (S4, and_1_out, and_2_out, and_3_out, and_4_out);
endmodule

module HEX5 (
  input  D3,
  input  D2,
  input  D1,
  input  D0,
  output S5
);

  wire and_1_out, and_2_out, and_3_out, and_4_out, and_5_out, not_1_out, not_2_out, not_3_out, not_4_out;

  not not_1 (not_1_out, D3);
  not not_2 (not_2_out, D2);
  not not_3 (not_3_out, D1);
  not not_4 (not_4_out, D0);
  and and_1 (and_1_out, not_1_out, not_3_out, not_4_out);
  and and_2 (and_2_out, not_1_out, D2, not_3_out);
  and and_3 (and_3_out, not_1_out, D2, not_4_out);
  and and_4 (and_4_out, D3, not_2_out);
  and and_5 (and_5_out, D3, D1);
  or or_1 (S5, and_1_out, and_2_out, and_3_out, and_4_out, and_5_out);
endmodule

module HEX0 (
  input  D3,
  input  D2,
  input  D1,
  input  D0,
  output s0
);

  wire and_1_out, and_2_out, and_3_out, and_4_out, and_5_out, not_1_out, not_2_out, not_3_out, not_4_out;

  not not_1 (not_1_out, D3);
  not not_2 (not_2_out, D2);
  not not_3 (not_3_out, D1);
  not not_4 (not_4_out, D0);
  and and_1 (and_1_out, not_2_out, not_4_out);
  and and_2 (and_2_out, not_1_out, D1);
  and and_3 (and_3_out, not_1_out, D2, D0);
  and and_4 (and_4_out, D2, D1);
  and and_5 (and_5_out, D3, not_2_out, not_3_out);
  or or_1 (s0, and_1_out, and_2_out, and_3_out, and_4_out, and_5_out);
endmodule

module HEX_DECODER (
  input  [3:0] in_1,
  output S0,
  output S1,
  output S2,
  output S3,
  output S4,
  output S5,
  output S6
);

  HEX0 hex0_1 (.D3(in_1[3]), .D2(in_1[2]), .D1(in_1[1]), .D0(in_1[0]), .s0(S0));
  HEX1 hex1_1 (.D3(in_1[3]), .D2(in_1[2]), .D1(in_1[1]), .D0(in_1[0]), .s1(S1));
  HEX2 hex2_1 (.D3(in_1[3]), .D2(in_1[2]), .D1(in_1[1]), .D0(in_1[0]), .S2(S2));
  HEX3 hex3_1 (.D3(in_1[3]), .D2(in_1[2]), .D1(in_1[1]), .D0(in_1[0]), .S3(S3));
  HEX4 hex4_1 (.D3(in_1[3]), .D2(in_1[2]), .D1(in_1[1]), .D0(in_1[0]), .S4(S4));
  HEX5 hex5_1 (.D3(in_1[3]), .D2(in_1[2]), .D1(in_1[1]), .D0(in_1[0]), .S5(S5));
  HEX6 hex6_1 (.D3(in_1[3]), .D2(in_1[2]), .D1(in_1[1]), .D0(in_1[0]), .S6(S6));
endmodule

module op6 (
  input  [3:0] A,
  input  [3:0] B,
  output [7:0] OPout
);

  wire [7:0] bit_extender_1_out;
  wire [8:0] bit_extender_2_out;
  wire [8:8] shifter_1_out;

  assign bit_extender_1_out = {{4{B[3]}}, B};  // Bit_Extender bit_extender_1
  assign bit_extender_2_out = {{1{1'b0}}, bit_extender_1_out};  // Bit_Extender bit_extender_2
  Shifter #(.shift("lr"), .width(9)) shifter_1 (.in(bit_extender_2_out), .\dist (A), .out({shifter_1_out[8], OPout}));
endmodule

module op7 (
  input  [3:0] A,
  input  [3:0] B,
  output [7:0] OPout
);

  Multiplier #(.width(4)) multiplier_1 (.a(A), .b(B), .out(OPout[3:0]), .cout(OPout[7:4]));  // open: cin
endmodule
