// Logisim project lab4_part2.circ as structural Verilog
module shifter_bit (
  input  Load,
  input  Reset,
  input  Sin,
  input  D,
  input  CLK,
  output Sout
);

  wire multiplexer_1_out;

  Multiplexer #(.enable("false")) multiplexer_1 (.in0(Sin), .in1(D), .out(multiplexer_1_out), .sel(Load));
  D_Flip_Flop d_ff_1 (.D(multiplexer_1_out), .clk(CLK), .Q(Sout), .reset(Reset));  // open: Qn, preset
endmodule

module shift_register (
  input  [7:0] D,
  input  Load,
  input  Reset,
  input  Sin,
  input  CLK,
  output Sout,
  output [7:0] Q
);

  shifter_bit shifter_bit_1 (.Load(Load), .Reset(Reset), .Sin(Sin), .D(D[7]), .CLK(CLK), .Sout(Q[7]));
  shifter_bit shifter_bit_2 (.Load(Load), .Reset(Reset), .Sin(Q[7]), .D(D[6]), .CLK(CLK), .Sout(Q[6]));
  shifter_bit shifter_bit_3 (.Load(Load), .Reset(Reset), .Sin(Q[6]), .D(D[5]), .CLK(CLK), .Sout(Q[5]));
  shifter_bit shifter_bit_4 (.Load(Load), .Reset(Reset), .Sin(Q[5]), .D(D[4]), .CLK(CLK), .Sout(Q[4]));
  shifter_bit shifter_bit_5 (.Load(Load), .Reset(Reset), .Sin(Q[4]), .D(D[3]), .CLK(CLK), .Sout(Q[3]));
  shifter_bit shifter_bit_6 (.Load(Load), .Reset(Reset), .Sin(Q[3]), .D(D[2]), .CLK(CLK), .Sout(Q[2]));
  shifter_bit shifter_bit_7 (.Load(Load), .Reset(Reset), .Sin(Q[2]), .D(D[1]), .CLK(CLK), .Sout(Q[1]));
  shifter_bit shifter_bit_8 (.Load(Load), .Reset(Reset), .Sin(Q[1]), .D(D[0]), .CLK(CLK), .Sout(Q[0]));

  assign Sout = Q[0];
endmodule

module bigger_shift_register (
  input  [15:0] D,
  input  Load,
  input  Reset,
  input  Sin,
  input  CLK,
  output [15:0] Q
);

  wire shift_register_1_sout;

  shift_register shift_register_1 (
    .D(D[15:8]), .Load(Load), .Reset(Reset), .Sin(Sin), .CLK(CLK), .Sout(shift_register_1_sout), .Q(Q[15:8]));
  shift_register shift_register_2 (
    .D(D[7:0]), .Load(Load), .Reset(Reset), .Sin(shift_register_1_sout), .CLK(CLK), .Q(Q[7:0]));  // open: Sout
endmodule
