// Logisim project lab5.circ as structural Verilog: 18 circuits, main circuit main
module main (
  input  SW3,
  input  SW2,
  input  SW1,
  input  SW0
);

  wire hex_decoder_1_s0, hex_decoder_1_s1, hex_decoder_1_s2, hex_decoder_1_s3, hex_decoder_1_s4,
       hex_decoder_1_s5, hex_decoder_1_s6;

  HEX_DECODER hex_decoder_1 (
    .D3(SW3), .D2(SW2), .D1(SW1), .D0(SW0), .S0(hex_decoder_1_s0), .S1(hex_decoder_1_s1),
    .S2(hex_decoder_1_s2), .S3(hex_decoder_1_s3), .S4(hex_decoder_1_s4), .S5(hex_decoder_1_s5),
    .S6(hex_decoder_1_s6));
  _7_Segment_Display u_7_segment_display_1 (
    .g(hex_decoder_1_s6), .f(hex_decoder_1_s5), .a(hex_decoder_1_s0), .b(hex_decoder_1_s1),
    .e(hex_decoder_1_s4), .d(hex_decoder_1_s3), .c(hex_decoder_1_s2));  // open: dp
endmodule

module incrementer4 (
  input  CountEnable,
  input  Clock,
  input  Clear,
  output [3:0] Q
);

  wire and_1_out, and_2_out, and_3_out;

  T_Flip_Flop TFF0 (.T(CountEnable), .clk(Clock), .Q(Q[0]), .reset(Clear));  // open: Qn, preset
  and and_1 (and_1_out, CountEnable, Q[0]);
  T_Flip_Flop TFF1 (.T(and_1_out), .clk(Clock), .Q(Q[1]), .reset(Clear));  // open: Qn, preset
  and and_2 (and_2_out, and_1_out, Q[1]);
  T_Flip_Flop TFF2 (.T(and_2_out), .clk(Clock), .Q(Q[2]), .reset(Clear));  // open: Qn, preset
  and and_3 (and_3_out, and_2_out, Q[2]);
  T_Flip_Flop TFF3 (.T(and_3_out), .clk(Clock), .Q(Q[3]), .reset(Clear));  // open: Qn, preset
endmodule

module handout_example (
  input  Reset,
  input  CountEnable,
  output CounterOut
);

  wire CLK_out, not_1_out, or_1_out;
  wire [3:0] counter_1_q;

  Clock CLK (.out(CLK_out));
  not not_1 (not_1_out, CountEnable);
  or or_1 (or_1_out, CounterOut, not_1_out);
  Counter #(.max('hf), .width(4)) counter_1 (
    .clr(Reset), .load(or_1_out), .up(1'b1), .clk(CLK_out), .D(4'b0000), .Q(counter_1_q));  // open: count, carry
  and and_1 (CounterOut, counter_1_q[0], counter_1_q[1], counter_1_q[2], counter_1_q[3]);
endmodule

module counter2 (
  input  CountEnable,
  input  [1:0] D,
  input  LoadEnable,
  input  Clock,
  input  Clear,
  output [1:0] Q
);

  wire and_1_out, multiplexer_1_out, multiplexer_2_out, xor_1_out, xor_2_out;

  xor xor_1 (xor_1_out, D[0], Q[0]);
  Multiplexer #(.enable("false")) multiplexer_1 (
    .in0(CountEnable), .in1(xor_1_out), .out(multiplexer_1_out), .sel(LoadEnable));
  T_Flip_Flop TFF0 (.T(multiplexer_1_out), .clk(Clock), .Q(Q[0]), .reset(Clear));  // open: Qn, preset
  and and_1 (and_1_out, multiplexer_1_out, Q[0]);
  xor xor_2 (xor_2_out, D[1], Q[1]);
  Multiplexer #(.enable("false")) multiplexer_2 (
    .in0(and_1_out), .in1(xor_2_out), .out(multiplexer_2_out), .sel(LoadEnable));
  T_Flip_Flop TFF1 (.T(multiplexer_2_out), .clk(Clock), .Q(Q[1]), .reset(Clear));  // open: Qn, preset
endmodule

module counter4 (
  input  CountEnable,
  input  [3:0] D,
  input  LoadEnable,
  input  Clock,
  input  Clear,
  output [3:0] Q
);

  wire and_1_out;

  counter2 counter2_1 (
    .CountEnable(CountEnable), .D(D[1:0]), .LoadEnable(LoadEnable), .Clock(Clock), .Clear(Clear), .Q(Q[1:0]));
  and and_1 (and_1_out, CountEnable, Q[0], Q[1]);
  counter2 counter2_2 (
    .CountEnable(and_1_out), .D(D[3:2]), .LoadEnable(LoadEnable), .Clock(Clock), .Clear(Clear), .Q(Q[3:2]));
endmodule

module counter8 (
  input  CountEnable,
  input  [7:0] D,
  input  LoadEnable,
  input  Clock,
  input  Clear,
  output [7:0] out_6
);

  wire and_1_out;

  counter4 counter4_1 (
    .CountEnable(CountEnable), .D(D[3:0]), .LoadEnable(LoadEnable), .Clock(Clock), .Clear(Clear),
    .Q(out_6[3:0]));
  and and_1 (and_1_out, CountEnable, out_6[0], out_6[1], out_6[2], out_6[3]);
  counter4 counter4_2 (
    .CountEnable(and_1_out), .D(D[7:4]), .LoadEnable(LoadEnable), .Clock(Clock), .Clear(Clear), .Q(out_6[7:4]));
endmodule

module rate_divider (
  input  [1:0] Rate,
  input  Enable,
  input  CLK,
  output DivOut
);

  wire and_1_out, and_2_out, and_3_out, and_4_out, multiplexer_1_out, not_1_out, or_1_out;
  wire [7:0] counter8_1_out_6;

  counter8 counter8_1 (.CountEnable(Enable), .Clock(CLK), .out_6(counter8_1_out_6));  // open: D, LoadEnable, Clear
  not not_1 (not_1_out, counter8_1_out_6[0]);
  and and_1 (and_1_out, Enable, not_1_out, counter8_1_out_6[1], counter8_1_out_6[2], counter8_1_out_6[3]);
  and and_2 (and_2_out, Enable, counter8_1_out_6[0], counter8_1_out_6[1], counter8_1_out_6[2], counter8_1_out_6[3]);
  or or_1 (or_1_out, and_1_out, and_2_out);
  and and_3 (and_3_out, or_1_out, counter8_1_out_6[4]);
  and and_4 (and_4_out, and_3_out, counter8_1_out_6[5]);
  Multiplexer #(.enable("false"), .select(2)) multiplexer_1 (
    .in0(Enable), .in1(or_1_out), .in2(and_3_out), .in3(and_4_out), .out(multiplexer_1_out), .sel(Rate));
  T_Flip_Flop t_ff_1 (.T(multiplexer_1_out), .clk(CLK), .Q(DivOut));  // open: Qn, reset, preset
endmodule

module MORSE_LUT (
  input  [2:0] Char,
  output [13:0] MorseCode
);

  Multiplexer #(.enable("false"), .select(3), .width(14)) multiplexer_1 (
    .in0(14'h2a00), .in1(14'h3800), .in2(14'h2b80), .in3(14'h2ae0), .in4(14'h2ee0), .in5(14'h3ab8),
    .in6(14'h3aee), .in7(14'h3ba8), .out(MorseCode), .sel(Char));
endmodule

module HEX6 (
  input  D3,
  input  D2,
  input  D1,
  input  D0,
  output S6
);

  wire and_1_out, and_2_out, and_3_out, not_1_out, not_2_out, not_3_out;

  not not_1 (not_1_out, D2);
  not not_2 (not_2_out, D1);
  not not_3 (not_3_out, D0);
  and and_1 (and_1_out, not_1_out, D1);
  and and_2 (and_2_out, D2, not_2_out);
  and and_3 (and_3_out, D2, not_3_out);
  or or_1 (S6, and_1_out, and_2_out, and_3_out, D3);
endmodule

module HEX1 (
  input  D3,
  input  D2,
  input  D1,
  input  D0,
  output s1
);

  wire and_1_out, and_2_out, and_3_out, and_4_out, and_5_out, not_1_out, not_2_out, not_3_out, not_4_out;

  not not_1 (not_1_out, D3);
  not not_2 (not_2_out, D2);
  not not_3 (not_3_out, D1);
  not not_4 (not_4_out, D0);
  and and_1 (and_1_out, not_1_out, not_2_out);
  and and_2 (and_2_out, not_1_out, not_3_out, not_4_out);
  and and_3 (and_3_out, not_2_out, not_4_out);
  and and_4 (and_4_out, not_1_out, D1, D0);
  and and_5 (and_5_out, D3, not_3_out, D0);
  or or_1 (s1, and_1_out, and_2_out, and_3_out, and_4_out, and_5_out);
endmodule

module HEX2 (
  input  D3,
  input  D2,
  input  D1,
  input  D0,
  output S2
);

  wire and_1_out, and_2_out, and_3_out, and_4_out, and_5_out, not_1_out, not_2_out, not_3_out;

  not not_1 (not_1_out, D3);
  not not_2 (not_2_out, D2);
  not not_3 (not_3_out, D1);
  and and_1 (and_1_out, not_2_out, not_3_out);
  and and_2 (and_2_out, not_2_out, D0);
  and and_3 (and_3_out, not_3_out, D0);
  and and_4 (and_4_out, not_1_out, D2);
  and and_5 (and_5_out, D3, not_2_out);
  or or_1 (S2, and_1_out, and_2_out, and_3_out, and_4_out, and_5_out);
endmodule

module HEX3 (
  input  D3,
  input  D2,
  input  D1,
  input  D0,
  output S3
);

  wire and_1_out, and_2_out, and_3_out, and_4_out, and_5_out, and_6_out, not_1_out, not_2_out, not_3_out,
       not_4_out;

  not not_1 (not_1_out, D3);
  not not_2 (not_2_out, D2);
  not not_3 (not_3_out, D1);
  not not_4 (not_4_out, D0);
  and and_1 (and_1_out, not_1_out, not_2_out, not_4_out);
  and and_2 (and_2_out, not_1_out, D1, not_4_out);
  and and_3 (and_3_out, not_2_out, D1, D0);
  and and_4 (and_4_out, D2, not_3_out, D0);
  and and_5 (and_5_out, D2, D1, not_4_out);
  and and_6 (and_6_out, D3, not_3_out);
  or or_1 (S3, and_1_out, and_2_out, and_3_out, and_4_out, and_5_out, and_6_out);
endmodule

module HEX4 (
  input  D3,
  input  D2,
  input  D1,
  input  D0,
  output S4
);

  wire and_1_out, and_2_out, and_3_out, and_4_out, not_1_out, not_2_out;

  not not_1 (not_1_out, D2);
  not not_2 (not_2_out, D0);
  and and_1 (and_1_out, not_1_out, not_2_out);
  and and_2 (and_2_out, D1, not_2_out);
  and and_3 (and_3_out, D3, D1);
  and and_4 (and_4_out, D3, D2);
  or or_1 (S4, and_1_out, and_2_out, and_3_out, and_4_out);
endmodule

module HEX5 (
  input  D3,
  input  D2,
  input  D1,
  input  D0,
  output S5
);

  wire and_1_out, and_2_out, and_3_out, and_4_out, and_5_out, not_1_out, not_2_out, not_3_out, not_4_out;

  not not_1 (not_1_out, D3);
  not not_2 (not_2_out, D2);
  not not_3 (not_3_out, D1);
  not not_4 (not_4_out, D0);
  and and_1 (and_1_out, not_1_out, not_3_out, not_4_out);
  and and_2 (and_2_out, not_1_out, D2, not_3_out);
  and and_3 (and_3_out, not_1_out, D2, not_4_out);
  and and_4 (and_4_out, D3, not_2_out);
  and and_5 (and_5_out, D3, D1);
  or or_1 (S5, and_1_out, and_2_out, and_3_out, and_4_out, and_5_out);
endmodule

module HEX0 (
  input  D3,
  input  D2,
  input  D1,
  input  D0,
  output s0
);

  wire and_1_out, and_2_out, and_3_out, and_4_out, and_5_out, not_1_out, not_2_out, not_3_out, not_4_out;

  not not_1 (not_1_out, D3);
  not not_2 (not_2_out, D2);
  not not_3 (not_3_out, D1);
  not not_4 (not_4_out, D0);
  and and_1 (and_1_out, not_2_out, not_4_out);
  and and_2 (and_2_out, not_1_out, D1);
  and and_3 (and_3_out, not_1_out, D2, D0);
  and and_4 (and_4_out, D2, D1);
  and and_5 (and_5_out, D3, not_2_out, not_3_out);
  or or_1 (s0, and_1_out, and_2_out, and_3_out, and_4_out, and_5_out);
endmodule

module HEX_DECODER (
  input  D3,
  input  D2,
  input  D1,
  input  D0,
  output S0,
  output S1,
  output S2,
  output S3,
  output S4,
  output S5,
  output S6
);

  HEX0 hex0_1 (.D3(D3), .D2(D2), .D1(D1), .D0(D0), .s0(S0));
  HEX1 hex1_1 (.D3(D3), .D2(D2), .D1(D1), .D0(D0), .s1(S1));
  HEX2 hex2_1 (.D3(D3), .D2(D2), .D1(D1), .D0(D0), .S2(S2));
  HEX3 hex3_1 (.D3(D3), .D2(D2), .D1(D1), .D0(D0), .S3(S3));
  HEX4 hex4_1 (.D3(D3), .D2(D2), .D1(D1), .D0(D0), .S4(S4));
  HEX5 hex5_1 (.D3(D3), .D2(D2), .D1(D1), .D0(D0), .S5(S5));
  HEX6 hex6_1 (.D3(D3), .D2(D2), .D1(D1), .D0(D0), .S6(S6));
endmodule

module demo_rate_divider (
  input  CountEnable,
  input  [1:0] Rate
);

  wire and_1_out, clock_1_out, hex_decoder_1_s0, hex_decoder_1_s1, hex_decoder_1_s2, hex_decoder_1_s3,
       hex_decoder_1_s4, hex_decoder_1_s5, hex_decoder_1_s6, hex_decoder_2_s0, hex_decoder_2_s1,
       hex_decoder_2_s2, hex_decoder_2_s3, hex_decoder_2_s4, hex_decoder_2_s5, hex_decoder_2_s6,
       rate_divider_1_divout;
  wire [3:0] GlobalSpeed_q, SlowerSpeed_q;

  Clock clock_1 (.out(clock_1_out));
  and and_1 (and_1_out, CountEnable, rate_divider_1_divout);
  rate_divider rate_divider_1 (.Rate(Rate), .Enable(1'b1), .CLK(clock_1_out), .DivOut(rate_divider_1_divout));
  counter4 GlobalSpeed (
    .CountEnable(CountEnable), .Clock(clock_1_out), .Q(GlobalSpeed_q));  // open: D, LoadEnable, Clear
  counter4 SlowerSpeed (.CountEnable(and_1_out), .Clock(clock_1_out), .Q(SlowerSpeed_q));  // open: D, LoadEnable, Clear
  HEX_DECODER hex_decoder_1 (
    .D3(GlobalSpeed_q[3]), .D2(GlobalSpeed_q[2]), .D1(GlobalSpeed_q[1]), .D0(GlobalSpeed_q[0]),
    .S0(hex_decoder_1_s0), .S1(hex_decoder_1_s1), .S2(hex_decoder_1_s2), .S3(hex_decoder_1_s3),
    .S4(hex_decoder_1_s4), .S5(hex_decoder_1_s5), .S6(hex_decoder_1_s6));
  HEX_DECODER hex_decoder_2 (
    .D3(SlowerSpeed_q[3]), .D2(SlowerSpeed_q[2]), .D1(SlowerSpeed_q[1]), .D0(SlowerSpeed_q[0]),
    .S0(hex_decoder_2_s0), .S1(hex_decoder_2_s1), .S2(hex_decoder_2_s2), .S3(hex_decoder_2_s3),
    .S4(hex_decoder_2_s4), .S5(hex_decoder_2_s5), .S6(hex_decoder_2_s6));
  _7_Segment_Display u_7_segment_display_1 (
    .g(hex_decoder_1_s6), .f(hex_decoder_1_s5), .a(hex_decoder_1_s0), .b(hex_decoder_1_s1),
    .e(hex_decoder_1_s4), .d(hex_decoder_1_s3), .c(hex_decoder_1_s2));  // open: dp
  _7_Segment_Display u_7_segment_display_2 (
    .g(hex_decoder_2_s6), .f(hex_decoder_2_s5), .a(hex_decoder_2_s0), .b(hex_decoder_2_s1),
    .e(hex_decoder_2_s4), .d(hex_decoder_2_s3), .c(hex_decoder_2_s2));  // open: dp
endmodule

module morse_code (
  input  LoadEnable,
  input  [2:0] CharSelect,
  input  [1:0] in_3,
  input  Enable
);

  wire clock_1_out, rate_divider_1_divout, undriven;
  wire [13:0] morse_lut_1_morsecode, multiplexer_1_out, register_1_q;

  Clock clock_1 (.out(clock_1_out));
  MORSE_LUT morse_lut_1 (.Char(CharSelect), .MorseCode(morse_lut_1_morsecode));
  rate_divider rate_divider_1 (.Rate(in_3), .Enable(Enable), .CLK(clock_1_out), .DivOut(rate_divider_1_divout));
  Multiplexer #(.enable("false"), .width(14)) multiplexer_1 (
    .in0({14{1'b0}}), .in1(morse_lut_1_morsecode), .out(multiplexer_1_out), .sel(LoadEnable));
  Register #(.width(14)) register_1 (
    .D(multiplexer_1_out), .en(rate_divider_1_divout), .clk(clock_1_out), .Q(register_1_q));  // open: clr
  // Shift_Register #(.length(14)) shift_register_1: pin names not known; wires that end beside it: LoadEnable, 1'b1, clock_1_out, register_1_q[0], register_1_q[1], register_1_q[2], register_1_q[3], register_1_q[4], register_1_q[5], register_1_q[6], register_1_q[7], register_1_q[8], register_1_q[9], register_1_q[10], register_1_q[11]
  LED led_1 (.in(undriven));
endmodule
