// Logisim project lab6_part1.circ as structural Verilog: 7 circuits, main circuit main
module main (
  input  W,
  input  CLK,
  input  Reset,
  output Z
);

  wire [6:0] correct_register_1_out_4, next_state_1_snext;

  Correct_register correct_register_1 (
    .S(next_state_1_snext), .CLK(CLK), .Reset(Reset), .out_4(correct_register_1_out_4));
  next_state next_state_1 (.S(correct_register_1_out_4), .W(W), .Snext(next_state_1_snext));
  output_logic output_logic_1 (.S(correct_register_1_out_4), .Z(Z));
endmodule

module next_state (
  input  [6:0] S,
  input  W,
  output [6:0] Snext
);

  wire not_1_out, or_1_out, or_2_out, or_3_out, or_4_out;

  not not_1 (not_1_out, W);
  and and_1 (Snext[3], S[2], W);
  or or_1 (or_1_out, S[0], S[1], S[4], S[6]);
  or or_2 (or_2_out, S[1], S[6]);
  or or_3 (or_3_out, S[2], S[3], S[5]);
  or or_4 (or_4_out, S[3], S[5]);
  and and_2 (Snext[6], S[4], W);
  and and_3 (Snext[2], or_2_out, W);
  and and_4 (Snext[4], or_3_out, not_1_out);
  and and_5 (Snext[5], or_4_out, W);
  and and_6 (Snext[0], or_1_out, not_1_out);
  and and_7 (Snext[1], S[0], W);
endmodule

module output_logic (
  input  [6:0] S,
  output Z
);

  or or_1 (Z, S[5], S[6]);
endmodule

module Rig (
  input  [6:0] S,
  input  Reset,
  input  Enable,
  input  CLK,
  output [6:0] out_5
);

  wire adder_1_cout, adder_1_out, adder_2_cout, adder_2_out, adder_3_cout, adder_3_out, adder_4_cout,
       adder_4_out, adder_5_cout, adder_5_out, adder_6_cout, adder_6_out, and_1_out, decoder_1_out0,
       nor_1_out, or_1_out;

  Adder #(.width(1)) adder_1 (.a(S[0]), .b(S[1]), .out(adder_1_out), .cout(adder_1_cout));  // open: cin
  Adder #(.width(1)) adder_2 (.a(adder_1_out), .b(S[2]), .out(adder_2_out), .cout(adder_2_cout));  // open: cin
  Adder #(.width(1)) adder_3 (.a(adder_2_out), .b(S[3]), .out(adder_3_out), .cout(adder_3_cout));  // open: cin
  Adder #(.width(1)) adder_4 (.a(adder_3_out), .b(S[4]), .out(adder_4_out), .cout(adder_4_cout));  // open: cin
  Adder #(.width(1)) adder_5 (.a(adder_4_out), .b(S[5]), .out(adder_5_out), .cout(adder_5_cout));  // open: cin
  Adder #(.width(1)) adder_6 (.a(adder_5_out), .b(S[6]), .out(adder_6_out), .cout(adder_6_cout));  // open: cin
  nor nor_1 (nor_1_out, adder_1_cout, adder_2_cout, adder_3_cout, adder_4_cout, adder_5_cout, adder_6_cout);
  and and_1 (and_1_out, adder_6_out, nor_1_out);
  Decoder decoder_1 (.out0(decoder_1_out0), .sel(and_1_out));  // open: out1, en
  Register #(.width(7)) register_1 (.D(S), .en(Enable), .clk(CLK), .Q(out_5), .clr(or_1_out));
  or or_1 (or_1_out, decoder_1_out0, Reset);
endmodule

module CheckValid (
  input  [6:0] S,
  output [6:0] out_2
);

  wire adder_1_cout, adder_1_out, adder_2_cout, adder_2_out, adder_3_cout, adder_3_out, adder_4_cout,
       adder_4_out, adder_5_cout, adder_5_out, adder_6_cout, adder_6_out, and_1_out, nor_1_out;

  Adder #(.width(1)) adder_1 (.a(S[0]), .b(S[1]), .out(adder_1_out), .cout(adder_1_cout));  // open: cin
  Adder #(.width(1)) adder_2 (.a(adder_1_out), .b(S[2]), .out(adder_2_out), .cout(adder_2_cout));  // open: cin
  Adder #(.width(1)) adder_3 (.a(adder_2_out), .b(S[3]), .out(adder_3_out), .cout(adder_3_cout));  // open: cin
  Adder #(.width(1)) adder_4 (.a(adder_3_out), .b(S[4]), .out(adder_4_out), .cout(adder_4_cout));  // open: cin
  Adder #(.width(1)) adder_5 (.a(adder_4_out), .b(S[5]), .out(adder_5_out), .cout(adder_5_cout));  // open: cin
  Adder #(.width(1)) adder_6 (.a(adder_5_out), .b(S[6]), .out(adder_6_out), .cout(adder_6_cout));  // open: cin
  nor nor_1 (nor_1_out, adder_1_cout, adder_2_cout, adder_3_cout, adder_4_cout, adder_5_cout, adder_6_cout);
  and and_1 (and_1_out, adder_6_out, nor_1_out);
  Multiplexer #(.enable("false"), .width(7)) multiplexer_1 (.in0(7'b0000001), .in1(S), .out(out_2), .sel(and_1_out));
endmodule

module State_Reg (
  input  [6:0] S,
  input  Enable,
  input  CLK,
  input  Reset,
  output [6:0] out_5
);

  wire nor_1_out;
  wire [6:0] register_1_q;

  Register #(.width(7)) register_1 (.D(S), .en(Enable), .clk(CLK), .Q(register_1_q), .clr(Reset));
  nor nor_1 (nor_1_out, register_1_q[0], register_1_q[1], register_1_q[2], register_1_q[3], register_1_q[4], register_1_q[5], register_1_q[6]);
  Multiplexer #(.enable("false"), .width(7)) multiplexer_1 (.in0(S), .in1(7'b0000001), .out(out_5), .sel(nor_1_out));
endmodule

module Correct_register (
  input  [6:0] S,
  input  CLK,
  input  Reset,
  output [6:0] out_4
);

  wire undriven;

  Register #(.width(6)) register_1 (.D(S[6:1]), .en(undriven), .clk(CLK), .Q(out_4[6:1]), .clr(Reset));
  D_Flip_Flop d_ff_1 (.D(S[0]), .clk(CLK), .Q(out_4[0]), .preset(Reset));  // open: Qn, reset
endmodule
