// Logisim project lab6_part3.circ as structural Verilog: 6 circuits, main circuit main
module main (
  input  [7:0] D,
  input  Reset
);

  wire CLK_out, controlunit_1_aluop, controlunit_1_loada, controlunit_1_loadaluout, controlunit_1_loadb,
       controlunit_1_loadc, controlunit_1_loadr, controlunit_1_loadx;
  wire [1:0] controlunit_1_alusela, controlunit_1_aluselb;
  wire [7:0] datapath_1_result;

  Clock CLK (.out(CLK_out));
  ControlUnit controlunit_1 (
    .Enable(1'b1), .CLK(CLK_out), .Reset(Reset), .ALUSelA(controlunit_1_alusela),
    .ALUSelB(controlunit_1_aluselb), .ALUop(controlunit_1_aluop), .LoadC(controlunit_1_loadc),
    .LoadX(controlunit_1_loadx), .LoadALUout(controlunit_1_loadaluout), .LoadA(controlunit_1_loada),
    .LoadB(controlunit_1_loadb), .LoadR(controlunit_1_loadr));
  Datapath datapath_1 (
    .D(D), .CLK(CLK_out), .ALUSelA(controlunit_1_alusela), .ALUSelB(controlunit_1_aluselb),
    .ALUop(controlunit_1_aluop), .LoadC(controlunit_1_loadc), .LoadX(controlunit_1_loadx),
    .LoadALUout(controlunit_1_loadaluout), .LoadA(controlunit_1_loada), .LoadB(controlunit_1_loadb),
    .LoadR(controlunit_1_loadr), .Reset(Reset), .Result(datapath_1_result));
  Hex_Digit_Display hex_digit_display_1 (.value(datapath_1_result[7:4]));  // open: dp
  Hex_Digit_Display hex_digit_display_2 (.value(datapath_1_result[3:0]));  // open: dp
endmodule

module ALU (
  input  [7:0] A,
  input  [7:0] B,
  input  op,
  output [7:0] ALUout
);

  wire [7:0] adder_1_out, multiplier_1_out;

  Adder adder_1 (.a(A), .b(B), .out(adder_1_out));  // open: cin, cout
  Multiplier multiplier_1 (.a(A), .b(B), .out(multiplier_1_out));  // open: cin, cout
  Multiplexer #(.enable("false"), .width(8)) multiplexer_1 (
    .in0(adder_1_out), .in1(multiplier_1_out), .out(ALUout), .sel(op));
endmodule

module Datapath (
  input  [7:0] D,
  input  CLK,
  input  [1:0] ALUSelA,
  input  [1:0] ALUSelB,
  input  ALUop,
  input  LoadC,
  input  LoadX,
  input  LoadALUout,
  input  LoadA,
  input  LoadB,
  input  LoadR,
  input  Reset,
  output [7:0] Result
);

  wire [7:0] alu_1_aluout, multiplexer_1_out, multiplexer_2_out, multiplexer_3_out, multiplexer_4_out,
       RegA_q, RegB_q, RegC_q, RegX_q;

  Multiplexer #(.enable("false"), .width(8)) multiplexer_1 (
    .in0(D), .in1(alu_1_aluout), .out(multiplexer_1_out), .sel(LoadALUout));
  Register RegC (.D(D), .en(LoadC), .clk(CLK), .Q(RegC_q), .clr(Reset));
  Register RegX (.D(D), .en(LoadX), .clk(CLK), .Q(RegX_q), .clr(Reset));
  Register RegA (.D(multiplexer_1_out), .en(LoadA), .clk(CLK), .Q(RegA_q), .clr(Reset));
  Register RegB (.D(multiplexer_2_out), .en(LoadB), .clk(CLK), .Q(RegB_q), .clr(Reset));
  Multiplexer #(.enable("false"), .width(8)) multiplexer_2 (
    .in0(D), .in1(alu_1_aluout), .out(multiplexer_2_out), .sel(LoadALUout));
  Register RegR (.D(alu_1_aluout), .en(LoadR), .clk(CLK), .Q(Result), .clr(Reset));
  Multiplexer #(.enable("false"), .select(2), .width(8)) multiplexer_3 (
    .in0(RegA_q), .in1(RegB_q), .in2(RegC_q), .in3(RegX_q), .out(multiplexer_3_out), .sel(ALUSelA));
  Multiplexer #(.enable("false"), .select(2), .width(8)) multiplexer_4 (
    .in0(RegA_q), .in1(RegB_q), .in2(RegC_q), .in3(RegX_q), .out(multiplexer_4_out), .sel(ALUSelB));
  ALU alu_1 (.A(multiplexer_3_out), .B(multiplexer_4_out), .op(ALUop), .ALUout(alu_1_aluout));
endmodule

module OutputLogic (
  input  [3:0] S,
  output [1:0] ALUSelA,
  output [1:0] ALUSelB,
  output ALUop,
  output LoadC,
  output LoadX,
  output LoadALUout,
  output LoadA,
  output LoadB,
  output LoadR
);

  wire and_4_out, and_5_out, and_6_out, and_7_out, and_8_out, and_12_out, and_13_out, and_14_out, and_15_out,
       not_1_out, not_2_out, not_3_out, not_4_out;

  not not_1 (not_1_out, S[3]);
  not not_2 (not_2_out, S[2]);
  not not_3 (not_3_out, S[1]);
  not not_4 (not_4_out, S[0]);
  and and_1 (ALUSelA[1], not_1_out, S[2], not_4_out);
  and and_2 (ALUSelA[0], not_1_out, S[2], not_4_out);
  and and_3 (ALUSelB[1], not_1_out, S[2], S[1]);
  and and_4 (and_4_out, not_1_out, S[2], not_3_out);
  and and_5 (and_5_out, not_1_out, S[2], not_4_out);
  or or_1 (ALUSelB[0], and_4_out, and_5_out, and_6_out);
  and and_6 (and_6_out, S[3], not_2_out, not_3_out, not_4_out);
  and and_7 (and_7_out, not_1_out, S[2], not_4_out);
  or or_2 (ALUop, and_7_out, and_8_out);
  and and_8 (and_8_out, not_1_out, S[2], S[1]);
  and and_9 (LoadC, not_1_out, not_2_out, S[1], not_4_out);
  and and_10 (LoadX, not_1_out, not_2_out, S[1], S[0]);
  and and_11 (LoadALUout, not_1_out, S[2]);
  and and_12 (and_12_out, not_1_out, not_2_out, not_3_out, not_4_out);
  or or_3 (LoadA, and_12_out, and_13_out);
  and and_13 (and_13_out, not_1_out, S[2], S[1]);
  and and_14 (and_14_out, not_1_out, not_3_out, S[0]);
  or or_4 (LoadB, and_14_out, and_15_out);
  and and_15 (and_15_out, not_1_out, S[2], not_3_out);
  and and_16 (LoadR, S[3], not_2_out, not_3_out, not_4_out);
endmodule

module NextStateLogic (
  input  [3:0] S,
  output [3:0] Snext
);

  wire and_2_out, and_3_out, and_4_out, and_5_out, and_6_out, not_1_out, not_2_out, not_3_out, not_4_out;

  not not_1 (not_1_out, S[3]);
  not not_2 (not_2_out, S[2]);
  not not_3 (not_3_out, S[1]);
  not not_4 (not_4_out, S[0]);
  and and_1 (Snext[3], not_1_out, S[2], S[1], S[0]);
  and and_2 (and_2_out, not_1_out, not_2_out, S[1], S[0]);
  and and_3 (and_3_out, not_1_out, S[2], not_3_out);
  or or_1 (Snext[2], and_2_out, and_3_out, and_4_out);
  and and_4 (and_4_out, not_1_out, S[2], not_4_out);
  and and_5 (and_5_out, not_1_out, not_3_out, S[0]);
  or or_2 (Snext[1], and_5_out, and_6_out);
  and and_6 (and_6_out, not_1_out, S[1], not_4_out);
  and and_7 (Snext[0], not_1_out, not_4_out);
endmodule

module ControlUnit (
  input  Enable,
  input  CLK,
  input  Reset,
  output [1:0] ALUSelA,
  output [1:0] ALUSelB,
  output ALUop,
  output LoadC,
  output LoadX,
  output LoadALUout,
  output LoadA,
  output LoadB,
  output LoadR
);

  wire [3:0] nextstatelogic_1_snext, RegState_q;

  NextStateLogic nextstatelogic_1 (.S(RegState_q), .Snext(nextstatelogic_1_snext));
  Register #(.width(4)) RegState (.D(nextstatelogic_1_snext), .en(Enable), .clk(CLK), .Q(RegState_q), .clr(Reset));
  OutputLogic outputlogic_1 (
    .S(RegState_q), .ALUSelA(ALUSelA), .ALUSelB(ALUSelB), .ALUop(ALUop), .LoadC(LoadC), .LoadX(LoadX),
    .LoadALUout(LoadALUout), .LoadA(LoadA), .LoadB(LoadB), .LoadR(LoadR));
endmodule
