// Logisim project lab7_demo.circ as structural Verilog: 6 circuits, main circuit main
module main (
  input  [6:0] X,
  input  [6:0] Y,
  input  Enable,
  input  Reset
);

  wire clock_1_out, controlunit_1_colorornot, controlunit_1_countenablex, controlunit_1_countenabley,
       controlunit_1_loadx, controlunit_1_loady;
  wire [6:0] datapath_1_outputx, datapath_1_outputy;
  wire [23:0] datapath_1_colour;

  Clock clock_1 (.out(clock_1_out));
  ControlUnit controlunit_1 (
    .Enable(Enable), .CLK(clock_1_out), .Reset(Reset), .LoadX(controlunit_1_loadx),
    .CountEnableX(controlunit_1_countenablex), .LoadY(controlunit_1_loady),
    .CountEnableY(controlunit_1_countenabley), .ColorOrNot(controlunit_1_colorornot));
  Datapath datapath_1 (
    .LoadX(controlunit_1_loadx), .X(X), .CountEnableX(controlunit_1_countenablex),
    .LoadY(controlunit_1_loady), .Y(Y), .CountEnableY(controlunit_1_countenabley),
    .ColorOrNot(controlunit_1_colorornot), .CLK(clock_1_out), .OutputX(datapath_1_outputx),
    .OutputY(datapath_1_outputy), .Colour(datapath_1_colour));
  // RGB_Video rgb_video_1: pin names not known; wires that end beside it: Reset, clock_1_out, Enable, datapath_1_outputx, datapath_1_outputy, datapath_1_colour
endmodule

module ControlUnit (
  input  Enable,
  input  CLK,
  input  Reset,
  output LoadX,
  output CountEnableX,
  output LoadY,
  output CountEnableY,
  output ColorOrNot
);

  wire [7:0] nextstatelogic_1_nextstate, register_1_q;

  NextStateLogic nextstatelogic_1 (.CurrentState(register_1_q), .NextState(nextstatelogic_1_nextstate));
  Register register_1 (.D(nextstatelogic_1_nextstate), .en(Enable), .clk(CLK), .Q(register_1_q), .clr(Reset));
  OutputLogic outputlogic_1 (
    .S(register_1_q), .LoadX(LoadX), .CountEnableX(CountEnableX), .LoadY(LoadY), .CountEnableY(CountEnableY),
    .ColorOrNot(ColorOrNot));
endmodule

module Datapath (
  input  LoadX,
  input  [6:0] X,
  input  CountEnableX,
  input  LoadY,
  input  [6:0] Y,
  input  CountEnableY,
  input  ColorOrNot,
  input  CLK,
  output [6:0] OutputX,
  output [6:0] OutputY,
  output [23:0] Colour
);

  wire counter_1_carry, t_ff_1_q;
  wire [23:0] multiplexer_1_out, register_1_q;

  Adder #(.width(7)) adder_1 (.b(X));  // open: a, out, cin, cout
  Register #(.width(24)) register_1 (.D(24'ha8d8ff), .clk(CLK), .Q(register_1_q));  // open: en, clr
  Counter counter_1 (.carry(counter_1_carry), .clk(CLK));  // open: load, D, count, Q, up, clr
  Counter #(.max('h7f), .width(7)) counter_2 (
    .load(LoadX), .count(CountEnableX), .Q(OutputX), .up(1'b1), .clk(CLK));  // open: D, carry, clr
  Counter #(.max('h7f), .width(7)) counter_3 (
    .load(LoadY), .D(Y), .count(CountEnableY), .Q(OutputY), .up(1'b1), .clk(CLK));  // open: carry, clr
  T_Flip_Flop t_ff_1 (.T(counter_1_carry), .clk(CLK), .Q(t_ff_1_q));  // open: Qn, reset, preset
  Multiplexer #(.enable("false"), .width(24)) multiplexer_1 (
    .in0({24{1'b0}}), .in1(register_1_q), .out(multiplexer_1_out), .sel(ColorOrNot));
  Multiplexer #(.enable("false"), .width(24)) multiplexer_2 (
    .in0(multiplexer_1_out), .in1({24{1'b0}}), .out(Colour), .sel(t_ff_1_q));
endmodule

module NextStateLogic (
  input  [7:0] CurrentState,
  output [7:0] NextState
);

  Adder adder_1 (.a(CurrentState), .b(8'h1), .out(NextState));  // open: cin, cout
endmodule

module OutputLogic (
  input  [7:0] S,
  output LoadX,
  output CountEnableX,
  output LoadY,
  output CountEnableY,
  output ColorOrNot
);

  wire not_1_out, not_2_out, not_3_out, not_4_out, not_5_out, not_6_out, not_7_out, not_8_out, not_9_out,
       or_2_out;

  not not_1 (not_1_out, S[0]);
  not not_2 (not_2_out, S[1]);
  not not_3 (not_3_out, S[2]);
  not not_4 (not_4_out, S[3]);
  not not_5 (not_5_out, S[4]);
  not not_6 (not_6_out, S[5]);
  not not_7 (not_7_out, S[6]);
  not not_8 (not_8_out, S[7]);
  or or_1 (ColorOrNot, S[0], S[1], S[2], S[3]);
  or or_2 (or_2_out, S[4], S[5], S[6], S[7]);
  and and_1 (LoadX, not_1_out, not_2_out, not_3_out, not_4_out, not_5_out, not_6_out, not_7_out, not_8_out);
  not not_9 (not_9_out, ColorOrNot);
  and and_2 (CountEnableX, not_9_out, or_2_out);
  or or_3 (LoadY, CountEnableX, LoadX);

  assign CountEnableY = ColorOrNot;
endmodule

module TrialDataPath (
  input  in_1,
  input  [6:0] in_2,
  input  in_3,
  input  in_4,
  input  [6:0] in_5,
  input  in_6,
  input  in_7,
  input  in_8,
  output [6:0] out_9,
  output [6:0] out_10,
  output [23:0] out_11
);

  wire [6:0] register_1_q, register_2_q;
  wire [23:0] register_3_q;

  Register #(.width(7)) register_1 (.D(in_2), .en(in_1), .clk(in_8), .Q(register_1_q));  // open: clr
  Register #(.width(7)) register_2 (.D(in_5), .en(in_4), .clk(in_8), .Q(register_2_q));  // open: clr
  Register #(.width(24)) register_3 (.D(24'ha8d8ff), .clk(in_8), .Q(register_3_q));  // open: en, clr
  Counter #(.max('h7f), .width(7)) counter_1 (
    .load(in_1), .D(register_1_q), .count(in_3), .Q(out_9), .up(1'b1), .clk(in_8));  // open: carry, clr
  Counter #(.max('h7f), .width(7)) counter_2 (
    .load(in_4), .D(register_2_q), .count(in_6), .Q(out_10), .up(1'b1), .clk(in_8));  // open: carry, clr
  Multiplexer #(.enable("false"), .width(24)) multiplexer_1 (
    .in0({24{1'b1}}), .in1(register_3_q), .out(out_11), .sel(in_7));
endmodule
