// Logisim project lab7_dom.circ as structural Verilog: 14 circuits, main circuit main
module main (
  input  [6:0] X,
  input  [6:0] Y,
  input  Enable,
  input  Reset,
  input  CLK
);

  wire domcontrolunit_1_draworerase, domcontrolunit_1_enablex, domcontrolunit_1_enabley,
       domcontrolunit_1_loadx, domcontrolunit_1_loady, domcontrolunit_1_o_enable, domdatapath_1_o_clk,
       domdatapath_1_o_enable, domdatapath_1_o_reset, fakeclk257_1_out_2;
  wire [6:0] domdatapath_1_o_x, domdatapath_1_o_y;
  wire [23:0] domdatapath_1_o_colour;

  DomControlUnit domcontrolunit_1 (
    .Enable(Enable), .CLK(fakeclk257_1_out_2), .Reset(Reset), .LoadX(domcontrolunit_1_loadx),
    .EnableX(domcontrolunit_1_enablex), .LoadY(domcontrolunit_1_loady), .EnableY(domcontrolunit_1_enabley),
    .O_Enable(domcontrolunit_1_o_enable), .DrawOrErase(domcontrolunit_1_draworerase));
  FakeCLK257 fakeclk257_1 (.CLK(CLK), .out_2(fakeclk257_1_out_2));
  DomDataPath domdatapath_1 (
    .LoadX(domcontrolunit_1_loadx), .X(X), .EnableX(domcontrolunit_1_enablex),
    .LoadY(domcontrolunit_1_loady), .Y(Y), .EnableY(domcontrolunit_1_enabley),
    .Enable(domcontrolunit_1_o_enable), .DrawOrErase(domcontrolunit_1_draworerase), .Reset(Reset), .CLK(CLK),
    .O_Reset(domdatapath_1_o_reset), .O_CLK(domdatapath_1_o_clk), .O_Enable(domdatapath_1_o_enable),
    .O_X(domdatapath_1_o_x), .O_Y(domdatapath_1_o_y), .O_Colour(domdatapath_1_o_colour));
  // RGB_Video rgb_video_1: pin names not known; wires that end beside it: domdatapath_1_o_reset, domdatapath_1_o_clk, domdatapath_1_o_enable, domdatapath_1_o_x, domdatapath_1_o_y, domdatapath_1_o_colour
endmodule

module ControlUnit (
  input  Enable,
  input  CLK,
  input  Reset,
  output LoadX,
  output CountEnableX,
  output LoadY,
  output CountEnableY,
  output ColorOrNot
);

  wire [7:0] nextstatelogic_1_nextstate, register_1_q;

  NextStateLogic nextstatelogic_1 (.CurrentState(register_1_q), .NextState(nextstatelogic_1_nextstate));
  Register register_1 (.D(nextstatelogic_1_nextstate), .en(Enable), .clk(CLK), .Q(register_1_q), .clr(Reset));
  OutputLogic outputlogic_1 (
    .S(register_1_q), .LoadX(LoadX), .CountEnableX(CountEnableX), .LoadY(LoadY), .CountEnableY(CountEnableY),
    .ColorOrNot(ColorOrNot));
endmodule

module Datapath (
  input  LoadX,
  input  [6:0] X,
  input  CountEnableX,
  input  LoadY,
  input  [6:0] Y,
  input  CountEnableY,
  input  ColorOrNot,
  input  DrawOrErase,
  input  CLK,
  output [6:0] OutputX,
  output [6:0] OutputY,
  output [23:0] Colour
);

  wire [23:0] multiplexer_1_out, register_1_q;

  Register #(.width(24)) register_1 (.D(24'ha8d8ff), .clk(CLK), .Q(register_1_q));  // open: en, clr
  Counter #(.max('h7f), .width(7)) counter_1 (
    .load(LoadX), .D(X), .count(CountEnableX), .Q(OutputX), .up(1'b1), .clk(CLK));  // open: carry, clr
  Counter #(.max('h7f), .width(7)) counter_2 (
    .load(LoadY), .D(Y), .count(CountEnableY), .Q(OutputY), .up(1'b1), .clk(CLK));  // open: carry, clr
  Multiplexer #(.enable("false"), .width(24)) multiplexer_1 (
    .in0({24{1'b0}}), .in1(register_1_q), .out(multiplexer_1_out), .sel(ColorOrNot));
  Multiplexer #(.enable("false"), .width(24)) multiplexer_2 (
    .in0({24{1'b0}}), .in1(multiplexer_1_out), .out(Colour), .sel(DrawOrErase));
endmodule

module NextStateLogic (
  input  [7:0] CurrentState,
  output [7:0] NextState
);

  Adder adder_1 (.a(CurrentState), .b(8'h1), .out(NextState));  // open: cin, cout
endmodule

module OutputLogic (
  input  [7:0] S,
  output LoadX,
  output CountEnableX,
  output LoadY,
  output CountEnableY,
  output ColorOrNot
);

  wire not_1_out, not_2_out, not_3_out, not_4_out, not_5_out, not_6_out, not_7_out, not_8_out, not_9_out,
       or_2_out;

  not not_1 (not_1_out, S[0]);
  not not_2 (not_2_out, S[1]);
  not not_3 (not_3_out, S[2]);
  not not_4 (not_4_out, S[3]);
  not not_5 (not_5_out, S[4]);
  not not_6 (not_6_out, S[5]);
  not not_7 (not_7_out, S[6]);
  not not_8 (not_8_out, S[7]);
  or or_1 (ColorOrNot, S[0], S[1], S[2], S[3]);
  or or_2 (or_2_out, S[4], S[5], S[6], S[7]);
  and and_1 (LoadX, not_1_out, not_2_out, not_3_out, not_4_out, not_5_out, not_6_out, not_7_out, not_8_out);
  not not_9 (not_9_out, ColorOrNot);
  and and_2 (CountEnableX, not_9_out, or_2_out);
  or or_3 (LoadY, CountEnableX, LoadX);

  assign CountEnableY = ColorOrNot;
endmodule

module TrialDataPath (
  input  in_1,
  input  [6:0] in_2,
  input  in_3,
  input  in_4,
  input  [6:0] in_5,
  input  in_6,
  input  in_7,
  input  in_8,
  output [6:0] out_9,
  output [6:0] out_10,
  output [23:0] out_11
);

  wire [6:0] register_1_q, register_2_q;
  wire [23:0] register_3_q;

  Register #(.width(7)) register_1 (.D(in_2), .en(in_1), .clk(in_8), .Q(register_1_q));  // open: clr
  Register #(.width(7)) register_2 (.D(in_5), .en(in_4), .clk(in_8), .Q(register_2_q));  // open: clr
  Register #(.width(24)) register_3 (.D(24'ha8d8ff), .clk(in_8), .Q(register_3_q));  // open: en, clr
  Counter #(.max('h7f), .width(7)) counter_1 (
    .load(in_1), .D(register_1_q), .count(in_3), .Q(out_9), .up(1'b1), .clk(in_8));  // open: carry, clr
  Counter #(.max('h7f), .width(7)) counter_2 (
    .load(in_4), .D(register_2_q), .count(in_6), .Q(out_10), .up(1'b1), .clk(in_8));  // open: carry, clr
  Multiplexer #(.enable("false"), .width(24)) multiplexer_1 (
    .in0({24{1'b1}}), .in1(register_3_q), .out(out_11), .sel(in_7));
endmodule

module DrawOrEraseAtXY (
  input  [6:0] X,
  input  [6:0] Y,
  input  Enable,
  input  DrawOrErase,
  input  CLK,
  input  Reset,
  output O_Reset,
  output O_CLK,
  output O_Enable,
  output [6:0] O_X,
  output [6:0] O_Y,
  output [23:0] O_Color
);

  wire controlunit_1_colorornot, controlunit_1_countenablex, controlunit_1_countenabley, controlunit_1_loadx,
       controlunit_1_loady;

  ControlUnit controlunit_1 (
    .Enable(Enable), .CLK(CLK), .Reset(Reset), .LoadX(controlunit_1_loadx),
    .CountEnableX(controlunit_1_countenablex), .LoadY(controlunit_1_loady),
    .CountEnableY(controlunit_1_countenabley), .ColorOrNot(controlunit_1_colorornot));
  Datapath datapath_1 (
    .LoadX(controlunit_1_loadx), .X(X), .CountEnableX(controlunit_1_countenablex),
    .LoadY(controlunit_1_loady), .Y(Y), .CountEnableY(controlunit_1_countenabley),
    .ColorOrNot(controlunit_1_colorornot), .DrawOrErase(DrawOrErase), .CLK(CLK), .OutputX(O_X),
    .OutputY(O_Y), .Colour(O_Color));

  assign O_CLK = CLK;
  assign O_Enable = Enable;
  assign O_Reset = Reset;
endmodule

module DomDataPath (
  input  LoadX,
  input  [6:0] X,
  input  EnableX,
  input  LoadY,
  input  [6:0] Y,
  input  EnableY,
  input  Enable,
  input  DrawOrErase,
  input  Reset,
  input  CLK,
  output O_Reset,
  output O_CLK,
  output O_Enable,
  output [6:0] O_X,
  output [6:0] O_Y,
  output [23:0] O_Colour
);

  wire [6:0] counter_1_q, counter_2_q;

  Counter #(.max('h7f), .width(7)) counter_1 (
    .load(LoadX), .D(X), .count(EnableX), .Q(counter_1_q), .up(1'b1), .clk(CLK));  // open: carry, clr
  Counter #(.max('h7f), .width(7)) counter_2 (
    .load(LoadY), .D(Y), .count(EnableY), .Q(counter_2_q), .up(1'b1), .clk(CLK));  // open: carry, clr
  DrawOrEraseAtXY draworeraseatxy_1 (
    .X(counter_1_q), .Y(counter_2_q), .Enable(Enable), .DrawOrErase(DrawOrErase), .CLK(CLK), .Reset(Reset),
    .O_Reset(O_Reset), .O_CLK(O_CLK), .O_Enable(O_Enable), .O_X(O_X), .O_Y(O_Y), .O_Color(O_Colour));
endmodule

module FakeCLK_256 (
  input  CLK,
  output out_2
);

  wire and_1_out;
  wire [7:0] counter_1_q;

  Counter counter_1 (.count(1'b1), .Q(counter_1_q), .up(1'b1), .clk(CLK));  // open: load, D, carry, clr
  and and_1 (and_1_out, counter_1_q[1], counter_1_q[2], counter_1_q[3], counter_1_q[4], counter_1_q[5], counter_1_q[6], counter_1_q[7]);
  T_Flip_Flop t_ff_1 (.T(and_1_out), .clk(CLK), .Q(out_2));  // open: Qn, reset, preset
endmodule

module DomControlUnit (
  input  Enable,
  input  CLK,
  input  Reset,
  output LoadX,
  output EnableX,
  output LoadY,
  output EnableY,
  output O_Enable,
  output DrawOrErase
);

  wire [1:0] demnextstate_1_x, register_1_q;

  DemNextState demnextstate_1 (.State(register_1_q), .x(demnextstate_1_x));
  Register #(.width(2)) register_1 (.D(demnextstate_1_x), .en(Enable), .clk(CLK), .Q(register_1_q), .clr(Reset));
  DomOutputLogic domoutputlogic_1 (
    .S(register_1_q), .LoadX(LoadX), .EnableX(EnableX), .LoadY(LoadY), .EnableY(EnableY), .Enable(O_Enable),
    .DrawOrErase(DrawOrErase));
endmodule

module DemNextState (
  input  [1:0] State,
  output [1:0] x
);

  wire and_1_out, and_2_out, not_1_out, not_2_out;

  not not_1 (not_1_out, State[1]);
  not not_2 (not_2_out, State[0]);
  and and_1 (and_1_out, not_1_out, State[0]);
  and and_2 (and_2_out, State[1], not_2_out);
  or or_1 (x[0], not_2_out, State[1]);
  or or_2 (x[1], and_1_out, and_2_out);
endmodule

module DomOutputLogic (
  input  [1:0] S,
  output LoadX,
  output EnableX,
  output LoadY,
  output EnableY,
  output Enable,
  output DrawOrErase
);

  wire and_5_out, and_6_out, not_1_out, not_2_out;

  not not_1 (not_1_out, S[1]);
  not not_2 (not_2_out, S[0]);
  and and_1 (LoadX, not_1_out, not_2_out);
  and and_2 (EnableX, S[1], S[0]);
  and and_3 (LoadY, not_1_out, not_2_out);
  and and_4 (EnableY, S[1], S[0]);
  and and_5 (and_5_out, not_1_out, S[0]);
  and and_6 (and_6_out, S[1], not_2_out);
  and and_7 (DrawOrErase, not_1_out, S[0]);
  or or_1 (Enable, and_5_out, and_6_out);
endmodule

module FakeCLK257NextState (
  input  [8:0] in_1,
  output [8:0] out_2
);

  wire subtractor_1_bout;
  wire [8:0] adder_1_out;

  Subtractor #(.width(9)) subtractor_1 (.a(in_1), .b(9'h100), .bout(subtractor_1_bout));  // open: out, bin
  Adder #(.width(9)) adder_1 (.a(in_1), .b(9'h1), .out(adder_1_out));  // open: cin, cout
  Multiplexer #(.enable("false"), .width(9)) multiplexer_1 (
    .in0({9{1'b0}}), .in1(adder_1_out), .out(out_2), .sel(subtractor_1_bout));
endmodule

module FakeCLK257 (
  input  CLK,
  output out_2
);

  wire and_1_out, and_2_out, nor_1_out, or_1_out;
  wire [8:0] fakeclk257nextstate_1_out_2, register_1_q;

  Register #(.width(9)) register_1 (.D(fakeclk257nextstate_1_out_2), .clk(CLK), .Q(register_1_q));  // open: en, clr
  FakeCLK257NextState fakeclk257nextstate_1 (.in_1(register_1_q), .out_2(fakeclk257nextstate_1_out_2));
  nor nor_1 (nor_1_out, register_1_q[0], register_1_q[1], register_1_q[2], register_1_q[3], register_1_q[4], register_1_q[5], register_1_q[6], register_1_q[7]);
  and and_1 (and_1_out, register_1_q[0], register_1_q[1], register_1_q[2], register_1_q[3], register_1_q[4], register_1_q[5], register_1_q[6], register_1_q[7]);
  and and_2 (and_2_out, nor_1_out, register_1_q[8]);
  or or_1 (or_1_out, and_1_out, and_2_out);
  T_Flip_Flop t_ff_1 (.T(or_1_out), .clk(CLK), .Q(out_2));  // open: Qn, reset, preset
endmodule
