// Logisim project lab7_part1.circ as structural Verilog: 2 circuits, main circuit main
module main (
  input  CLK
);

  wire memorywriter_1_done, not_1_out;
  wire [3:0] memorywriter_1_value;
  wire [4:0] memorywriter_1_address;

  MemoryWriter memorywriter_1 (
    .CLK(CLK), .Done(memorywriter_1_done), .Address(memorywriter_1_address), .Value(memorywriter_1_value));
  not not_1 (not_1_out, memorywriter_1_done);
  RAM #(.addrWidth(5), .dataWidth(4)) ram_1 (
    .addr(memorywriter_1_address), .we(not_1_out), .clk(CLK), .din(memorywriter_1_value));  // open: oe, dout
endmodule

module MemoryWriter (
  input  CLK,
  output Done,
  output [4:0] Address,
  output [3:0] Value
);

  wire counter_1_carry;

  Counter #(.max('h1f), .width(5)) counter_1 (
    .up(1'b1), .clk(CLK), .carry(counter_1_carry), .Q(Address));  // open: clr, load, count, D
  D_Flip_Flop d_ff_1 (.D(counter_1_carry), .clk(CLK), .Q(Done), .preset(Done));  // open: Qn, reset

  assign Value = Address[3:0];
endmodule
